# Fritzing sketch ledmatrixmodule (saved by Fritzing 0.9.3b)
breadboards: 1

parts:
  NI = longpad pin header, 34 pins [form="long pad"]
  J1 = longpad pin header, 7 pins [form="long pad"]
  J2 = longpad pin header, 7 pins [form="long pad"]
  J3 = longpad pin header, 7 pins [form="long pad"]
  J4 = longpad pin header, 7 pins [form="long pad"]  # not connected
  J5 = longpad pin header, 7 pins [form="long pad"]  # not connected
  J6 = longpad pin header, 7 pins [form="long pad"]  # not connected
  J7 = longpad pin header, 7 pins [form="long pad"]  # not connected
  J8 = longpad pin header, 7 pins [form="long pad"]  # not connected
  J9 = longpad pin header, 7 pins [form="long pad"]
  J10 = longpad pin header, 7 pins [form="long pad"]  # not connected
  J11 = longpad pin header, 7 pins [form="long pad"]  # not connected
  J12 = longpad pin header, 7 pins [form="long pad"]  # not connected
  J13 = longpad pin header, 7 pins [form="long pad"]  # not connected
  J14 = longpad pin header, 7 pins [form="long pad"]  # not connected
  J15 = longpad pin header, 7 pins [form="long pad"]  # not connected
  U4 = IC, DIP package, 20 pins [chip_label=74HC373]
  U5 = IC, DIP package, 20 pins [chip_label=74HC373]  # not connected
  U20 = IC, DIP package, 20 pins [chip_label=74HC373]  # not connected
  U6 = IC, DIP package, 20 pins [chip_label=74HC373]  # not connected
  U15 = IC, DIP package, 16 pins [chip_label=74HC237B]
  U25 = IC, DIP package, 16 pins [chip_label=ULN2003A]
  U24 = IC, DIP package, 16 pins [chip_label=ULN2003A]  # not connected
  KINGBRIGHT = IC, DIP package, 14 pins [chip_label=ta20-11ewa]  # not connected
  KINGBRIGHT1 = IC, DIP package, 14 pins [chip_label=ta20-11ewa]  # not connected

nets:
  N1: NI.pin1, NI.pin10
  N2: NI.pin11, U4.pin17
  N3: NI.pin12, U4.pin18
  N4: NI.pin13, U4.pin13
  N5: NI.pin14, U4.pin14
  N6: NI.pin15, U4.pin7
  N7: NI.pin16, U4.pin8
  N8: NI.pin17, U4.pin3
  N9: NI.pin18, U4.pin4
  pin12 U22: NI.pin20
  N10: NI.pin22, U15.pin2
  pin15 U22: NI.pin23
  N11: NI.pin25, U15.pin1
  N12: NI.pin26, U15.pin3
  N13: NI.pin27, NI.pin34
  N14: J1.pin3, U4.pin9
  N15: J1.pin6, U4.pin2
  N16: J2.pin3, U4.pin5
  N17: J2.pin4, U4.pin6
  N18: J2.pin6, U4.pin12
  N19: J3.pin2, U4.pin15
  N20: J9.pin3, U4.pin16
  N21: J9.pin4, U4.pin19
  N22: U15.pin7, U25.pin7
  N23: U15.pin8, U25.pin8
  N24: U15.pin9, U25.pin6
  N25: U15.pin10, U25.pin5
  N26: U15.pin11, U25.pin4
  N27: U15.pin12, U25.pin3
  N28: U15.pin13, U25.pin2
  N29: U15.pin14, U25.pin1

notes:
  COMPONENT SIDE
  LEISURE UNLIMITED LU-A161
  LEDM1
  follow IDE pin numbering
  convention
  LEDM2
  LEDM3
  LEDM4
  LEDM5
  kingbright ta20-11ewa
  LED display
  (5x7 14-pin)
